# Fritzing sketch Panobot Plan (saved by Fritzing 0.7.1b)
breadboards: 1

parts:
  Arduino1 = Arduino
  Bauteil1 = DeuLigne 1.1 - The Snootlab's LCD shield for Arduino
  Bauteil2 = Arduino USB Host Shield
  U2 = Voltage Regulator - 5V [package="TO220 [THT]"]
  C3 = Electrolytic Capacitor [capacitance=100nF rated_voltage=35V package="100 mil [THT, electrolytic]"]
  C4 = Electrolytic Capacitor [capacitance=100nF rated_voltage=35V package="100 mil [THT, electrolytic]"]
  J4 = female pin header, 2 pins [form="♂ (male)"]
  VCC1 = Battery block 9V
  J5 = Basic Servo
  J6 = Basic Servo
  IC1 = IC, DIP package, 16 pins [chip_label="Servo Controler" spacing=300mil]

nets:
  N1: Arduino1.D10, Bauteil2.SS
  N2: Arduino1.D9, Bauteil2.INT
  +5V: Arduino1.+5V, Bauteil1.+5V, Bauteil2.5V-ARDUINO, U2.output_voltage, C3.+, J4.pin1, J5.vcc, J6.vcc, IC1.pin9, IC1.pin15
  GND: Arduino1.GND, Bauteil1.GND, Bauteil2.GND, U2.GND, C3.-, C4.-, J4.pin2, VCC1.-, J5.gnd, J6.gnd, IC1.pin10, IC1.pin16
  N3: Arduino1.A4, Bauteil1.A4(SDA)
  N4: Arduino1.A5, Bauteil1.A5(CLK)
  N5: Bauteil2.D2, IC1.pin14
  N6: Bauteil2.D3, IC1.pin13
  N7: Bauteil2.D4, IC1.pin12
  N8: U2.input_voltage, C4.+, VCC1.+
  N9: J5.pulse, IC1.pin2
  N10: J6.pulse, IC1.pin1

notes:
  Verwende das adafruit RGB LCD Display Shield
